// Logisim project 2024_2025_Trabajo_Ruta_Datos.circ as structural Verilog: 4 circuits, main circuit main
module main (
  input  LAIN,
  input  LAC,
  input  [1:0] SX,
  input  LI,
  input  TI,
  input  SMEM,
  input  LA,
  input  TMR,
  input  WMEM,
  input  TAC,
  input  [1:0] SY,
  input  LP,
  input  TP,
  input  R_W_prime,
  input  LD,
  input  TMW,
  input  TALU1,
  input  CLR,
  input  [3:0] SOP,
  input  LS,
  input  TS,
  input  TALU2
);

  wire alu_1_out_13, alu_1_out_14;
  wire [3:0] TALU1_out, TALU1_out_2, TALU1_out_3, TALU1_out_4, TI_out, TI_out_2, TI_out_3;
  wire [15:0] AC, alu_1_resultado, and_1_out, banco_registros_1_a_out, banco_registros_1_b_out, MAR, MDR, PC,
       ram_1_data, RI, SP;
  wire [15:12] TI_out_4;

  Hex_Digit_Display hex_digit_display_1 (.value(TI_out_3));  // open: dp
  Hex_Digit_Display hex_digit_display_2 (.value(TI_out_4));  // open: dp
  Banco_Registros banco_registros_1 (
    .LAIN(LAIN), .A_OUT(banco_registros_1_a_out), .B_OUT(banco_registros_1_b_out),
    .A_IN({TI_out_4, TI_out_3, TI_out_2, TI_out}), .SEL_A(RI[11:9]), .SEL_B(RI[8:6]));
  Hex_Digit_Display hex_digit_display_3 (.value(TI_out));  // open: dp
  Hex_Digit_Display hex_digit_display_4 (.value(TI_out_2));  // open: dp
  Hex_Digit_Display hex_digit_display_5 (.value(banco_registros_1_a_out[15:12]));  // open: dp
  Hex_Digit_Display hex_digit_display_6 (.value(banco_registros_1_b_out[15:12]));  // open: dp
  Hex_Digit_Display hex_digit_display_7 (.value(banco_registros_1_a_out[7:4]));  // open: dp
  Hex_Digit_Display hex_digit_display_8 (.value(banco_registros_1_a_out[11:8]));  // open: dp
  Hex_Digit_Display hex_digit_display_9 (.value(banco_registros_1_b_out[7:4]));  // open: dp
  Hex_Digit_Display hex_digit_display_10 (.value(banco_registros_1_b_out[11:8]));  // open: dp
  Hex_Digit_Display hex_digit_display_11 (.value(banco_registros_1_a_out[3:0]));  // open: dp
  Hex_Digit_Display hex_digit_display_12 (.value(banco_registros_1_b_out[3:0]));  // open: dp
  Register #(.width(16), .trigger("falling")) u_RI (
    .D({TI_out_4, TI_out_3, TI_out_2, TI_out}), .Q(RI), .clk(LI));  // open: en, clr
  ALU alu_1 (
    .MUX_X_0(AC), .MUX_X_1(PC), .MUX_X_2(banco_registros_1_a_out), .MUX_X_3(banco_registros_1_b_out),
    .MUX_Y_0({TI_out_4, TI_out_3, TI_out_2, TI_out}), .MUX_Y_1(SP), .MUX_Y_2(banco_registros_1_a_out),
    .MUX_Y_3(banco_registros_1_b_out), .SOP(SOP), .Resultado(alu_1_resultado), .out_13(alu_1_out_13),
    .SY(SY), .SX(SX), .out_14(alu_1_out_14));
  assign and_1_out = 16'h3f & RI;  // AND_Gate and_1, 16 bits wide
  assign {TI_out_4, TI_out_3, TI_out_2, TI_out} = TI ? and_1_out : 16'bz;  // Controlled_Buffer TI
  assign {TALU1_out_4, TALU1_out_3, TALU1_out_2, TALU1_out} = TALU1 ? alu_1_resultado : 16'bz;  // Controlled_Buffer TALU1
  LED led_1 (.in(alu_1_out_13));
  LED led_2 (.in(alu_1_out_14));
  assign {TI_out_4, TI_out_3, TI_out_2, TI_out} = TALU2 ? alu_1_resultado : 16'bz;  // Controlled_Buffer TALU2
  Hex_Digit_Display hex_digit_display_13 (.value(alu_1_resultado[11:8]));  // open: dp
  Hex_Digit_Display hex_digit_display_14 (.value(alu_1_resultado[15:12]));  // open: dp
  Hex_Digit_Display hex_digit_display_15 (.value(alu_1_resultado[3:0]));  // open: dp
  Hex_Digit_Display hex_digit_display_16 (.value(alu_1_resultado[7:4]));  // open: dp
  Register #(.width(16), .trigger("falling")) u_AC (.D(alu_1_resultado), .Q(AC), .clk(LAC));  // open: en, clr
  assign {TI_out_4, TI_out_3, TI_out_2, TI_out} = TAC ? AC : 16'bz;  // Controlled_Buffer TAC
  Register #(.width(16), .trigger("falling")) u_PC (
    .D({TALU1_out_4, TALU1_out_3, TALU1_out_2, TALU1_out}), .Q(PC), .clk(LP));  // open: en, clr
  Register #(.width(16), .trigger("falling")) u_MAR (
    .D({TALU1_out_4, TALU1_out_3, TALU1_out_2, TALU1_out}), .Q(MAR), .clk(LA));  // open: en, clr
  assign {TALU1_out_4, TALU1_out_3, TALU1_out_2, TALU1_out} = TP ? PC : 16'bz;  // Controlled_Buffer TP
  Register #(.width(16), .trigger("falling")) u_SP (
    .D({TALU1_out_4, TALU1_out_3, TALU1_out_2, TALU1_out}), .Q(SP), .clk(LS));  // open: en, clr
  Hex_Digit_Display hex_digit_display_17 (.value(ram_1_data[15:12]));  // open: dp
  RAM #(.addrWidth(16), .dataWidth(16)) ram_1 (
    .addr(MAR), .data(ram_1_data), .sel(SMEM), .clk(WMEM), .ld(R_W_prime), .clr(CLR));
  assign ram_1_data = TMW ? {TI_out_4, TI_out_3, TI_out_2, TI_out} : 16'bz;  // Controlled_Buffer TMW
  assign {TALU1_out_4, TALU1_out_3, TALU1_out_2, TALU1_out} = TS ? SP : 16'bz;  // Controlled_Buffer TP_2
  Hex_Digit_Display hex_digit_display_18 (.value(ram_1_data[7:4]));  // open: dp
  Hex_Digit_Display hex_digit_display_19 (.value(ram_1_data[11:8]));  // open: dp
  Register #(.width(16), .trigger("falling")) u_MDR (.D(ram_1_data), .Q(MDR), .clk(LD));  // open: en, clr
  assign {TI_out_4, TI_out_3, TI_out_2, TI_out} = TMR ? MDR : 16'bz;  // Controlled_Buffer TMR
  Hex_Digit_Display hex_digit_display_20 (.value(TALU1_out_3));  // open: dp
  Hex_Digit_Display hex_digit_display_21 (.value(TALU1_out_4));  // open: dp
  Hex_Digit_Display hex_digit_display_22 (.value(ram_1_data[3:0]));  // open: dp
  Hex_Digit_Display hex_digit_display_23 (.value(TALU1_out_2));  // open: dp
  Hex_Digit_Display hex_digit_display_24 (.value(TALU1_out));  // open: dp

  // Other names for the same wires on the sheet: SEL_A[2:0] = RI[11:9]; SEL_B[2:0] = RI[8:6]

  // Notes on the sheet:
  //   RUTA DE DATOS
  //   SEÑALES DE CONTROL
  //   BUS DE DIRECCIONES (16 BITS)
  //   BUS DE DATOS (16 BITS)
  //   BANCO DE REGISTROS
  //   UNIDAD ARITMÉTICO-LÓGICA
  //   REGISTROS ESPECIALES
  //   MEMORIA
endmodule

module Banco_Registros (
  input  LAIN,
  input  [15:0] A_IN,
  input  [2:0] SEL_A,
  input  [2:0] SEL_B,
  output [15:0] A_OUT,
  output [15:0] B_OUT
);

  wire and_1_out, and_2_out, and_3_out, and_4_out, and_5_out, and_6_out, and_7_out, and_8_out,
       decoder_1_out0, decoder_1_out1, decoder_1_out2, decoder_1_out3, decoder_1_out4, decoder_1_out5,
       decoder_1_out6, decoder_1_out7;
  wire [15:0] R0_q, R1_q, R2_q, R3_q, R4_q, R5_q, R6_q, R7_q;

  Decoder #(.select(3)) decoder_1 (
    .out0(decoder_1_out0), .out1(decoder_1_out1), .out2(decoder_1_out2), .out3(decoder_1_out3),
    .out4(decoder_1_out4), .out5(decoder_1_out5), .out6(decoder_1_out6), .out7(decoder_1_out7), .sel(SEL_A));  // open: en
  and and_1 (and_1_out, LAIN, decoder_1_out0);
  and and_2 (and_2_out, LAIN, decoder_1_out1);
  and and_3 (and_3_out, LAIN, decoder_1_out2);
  and and_4 (and_4_out, LAIN, decoder_1_out3);
  and and_5 (and_5_out, LAIN, decoder_1_out4);
  and and_6 (and_6_out, LAIN, decoder_1_out5);
  and and_7 (and_7_out, LAIN, decoder_1_out6);
  and and_8 (and_8_out, LAIN, decoder_1_out7);
  Register #(.width(16), .trigger("falling")) R0 (.D(A_IN), .Q(R0_q), .clk(and_1_out));  // open: en, clr
  Register #(.width(16), .trigger("falling")) R1 (.D(A_IN), .Q(R1_q), .clk(and_2_out));  // open: en, clr
  Register #(.width(16), .trigger("falling")) R2 (.D(A_IN), .Q(R2_q), .clk(and_3_out));  // open: en, clr
  Register #(.width(16), .trigger("falling")) R3 (.D(A_IN), .Q(R3_q), .clk(and_4_out));  // open: en, clr
  Register #(.width(16), .trigger("falling")) R4 (.D(A_IN), .Q(R4_q), .clk(and_5_out));  // open: en, clr
  Register #(.width(16), .trigger("falling")) R5 (.D(A_IN), .Q(R5_q), .clk(and_6_out));  // open: en, clr
  Register #(.width(16), .trigger("falling")) R6 (.D(A_IN), .Q(R6_q), .clk(and_7_out));  // open: en, clr
  Register #(.width(16), .trigger("falling")) R7 (.D(A_IN), .Q(R7_q), .clk(and_8_out));  // open: en, clr
  Multiplexer #(.select(3), .width(16)) multiplexer_1 (
    .in0(R0_q), .in1(R1_q), .in2(R2_q), .in3(R3_q), .in4(R4_q), .in5(R5_q), .in6(R6_q), .in7(R7_q),
    .out(A_OUT), .sel(SEL_A));  // open: en
  Multiplexer #(.select(3), .width(16)) multiplexer_2 (
    .in0(R0_q), .in1(R1_q), .in2(R2_q), .in3(R3_q), .in4(R4_q), .in5(R5_q), .in6(R6_q), .in7(R7_q),
    .out(B_OUT), .sel(SEL_B));  // open: en
endmodule

module ALU (
  input  [15:0] MUX_X_0,
  input  [15:0] MUX_X_1,
  input  [15:0] MUX_X_2,
  input  [15:0] MUX_X_3,
  input  [15:0] MUX_Y_0,
  input  [15:0] MUX_Y_1,
  input  [15:0] MUX_Y_2,
  input  [15:0] MUX_Y_3,
  input  [1:0] SY,
  input  [1:0] SX,
  input  [3:0] SOP,
  output [15:0] Resultado,
  output out_13,
  output out_14
);

  wire [15:0] multiplexer_1_out, multiplexer_2_out;

  Multiplexer #(.select(2), .width(16)) multiplexer_1 (
    .in0(MUX_Y_0), .in1(MUX_Y_1), .in2(MUX_Y_2), .in3(MUX_Y_3), .out(multiplexer_1_out), .sel(SY));  // open: en
  Multiplexer #(.select(2), .width(16)) multiplexer_2 (
    .in0(MUX_X_0), .in1(MUX_X_1), .in2(MUX_X_2), .in3(MUX_X_3), .out(multiplexer_2_out), .sel(SX));  // open: en
  // Probe on multiplexer_2_out
  // Probe on multiplexer_1_out
  Operaciones operaciones_1 (
    .Operando_1(multiplexer_2_out), .Operando_2(multiplexer_1_out), .Seleccion_Operacion(SOP),
    .Resultado(Resultado), .Flag_Z(out_13), .Flag_Carry(out_14));
  LED led_1 (.in(out_13));
  LED led_2 (.in(out_14));

  // Notes on the sheet:
  //   ALU
  //   Banco de Registros
  //   Selección Operandos
  //   Selección Operación
  //   Circuitos lógicos y aritméticos
  //   Resultado y Flags
endmodule

module Operaciones (
  input  [15:0] Operando_1,
  input  [15:0] Operando_2,
  input  [3:0] Seleccion_Operacion,
  output [15:0] Resultado,
  output Flag_Z,
  output Flag_Carry
);

  wire adder_1_cout, adder_2_cout, adder_3_cout, subtractor_1_bout, subtractor_2_bout, subtractor_3_bout;
  wire [15:0] adder_1_out, adder_2_out, adder_3_out, and_1_out, nand_1_out, nor_1_out, not_1_out, not_2_out,
       or_1_out, subtractor_1_out, subtractor_2_out, subtractor_3_out;

  Adder #(.width(16)) adder_1 (.a(Operando_1), .b(16'h1), .out(adder_1_out), .cout(adder_1_cout));  // open: cin
  Subtractor #(.width(16)) subtractor_1 (
    .a(Operando_1), .b(16'h1), .out(subtractor_1_out), .bout(subtractor_1_bout));  // open: bin
  Adder #(.width(16)) adder_2 (.a(Operando_2), .b(16'h1), .out(adder_2_out), .cout(adder_2_cout));  // open: cin
  Subtractor #(.width(16)) subtractor_2 (
    .a(Operando_2), .b(16'h1), .out(subtractor_2_out), .bout(subtractor_2_bout));  // open: bin
  Adder #(.width(16)) adder_3 (.a(Operando_1), .b(Operando_2), .out(adder_3_out), .cout(adder_3_cout));  // open: cin
  Subtractor #(.width(16)) subtractor_3 (
    .a(Operando_1), .b(Operando_2), .out(subtractor_3_out), .bout(subtractor_3_bout));  // open: bin
  assign and_1_out = Operando_1 & Operando_2;  // AND_Gate and_1, 16 bits wide
  assign or_1_out = Operando_1 | Operando_2;  // OR_Gate or_1, 16 bits wide
  assign not_1_out = ~Operando_1;  // NOT_Gate not_1, 16 bits wide
  assign not_2_out = ~Operando_2;  // NOT_Gate not_2, 16 bits wide
  assign nand_1_out = ~(Operando_1 & Operando_2);  // NAND_Gate nand_1, 16 bits wide
  assign nor_1_out = ~(Operando_1 | Operando_2);  // NOR_Gate nor_1, 16 bits wide
  Multiplexer #(.select(4), .width(16)) multiplexer_1 (
    .in0(Operando_1), .in1(Operando_2), .in2(adder_1_out), .in3(subtractor_1_out), .in4(adder_2_out),
    .in5(subtractor_2_out), .in6(adder_3_out), .in7(subtractor_3_out), .in8(nand_1_out), .in9(nor_1_out),
    .in10(and_1_out), .in11(or_1_out), .in12(not_1_out), .in13(not_2_out), .out(Resultado),
    .sel(Seleccion_Operacion));  // open: in14, in15, en
  nor nor_2 (Flag_Z, Resultado[0], Resultado[1], Resultado[2], Resultado[3], Resultado[4], Resultado[5], Resultado[6], Resultado[7], Resultado[8], Resultado[9], Resultado[10], Resultado[11], Resultado[12], Resultado[13], Resultado[14], Resultado[15]);
  Multiplexer #(.select(4)) multiplexer_2 (
    .in2(adder_1_cout), .in3(subtractor_1_bout), .in4(adder_2_cout), .in5(subtractor_2_bout),
    .in6(adder_3_cout), .in7(subtractor_3_bout), .out(Flag_Carry), .sel(Seleccion_Operacion));  // open: in0, in1, in8, in9, in10, in11, in12, in13, in14, in15, en
endmodule
