// Logisim project Trabajo Logisim.circ as structural Verilog: 1 circuit, main circuit main
module main (
  input  [15:0] Direccion,
  input  [15:0] MDR__Memory_Data_Register,
  input  R_W_prime,
  input  Clear
);

  wire and_1_out, and_2_out, decoder_1_out0, decoder_1_out1, decoder_1_out2, decoder_1_out3, not_1_out;
  wire [7:0] ram_1_data, rom_1_data;

  // Probe on Direccion
  Decoder #(.select(2), .enable("false")) decoder_1 (
    .out0(decoder_1_out0), .out1(decoder_1_out1), .out2(decoder_1_out2), .out3(decoder_1_out3),
    .sel(Direccion[15:14]));
  and and_1 (and_1_out, R_W_prime, decoder_1_out0);
  and and_2 (and_2_out, R_W_prime, decoder_1_out1);
  // Probe on Direccion[13:0]
  RAM #(.addrWidth(14)) ram_1 (
    .addr(Direccion[13:0]), .data(ram_1_data), .sel(decoder_1_out3), .ld(R_W_prime), .clr(Clear));  // open: clk
  RAM #(.addrWidth(14)) ram_2 (
    .addr(Direccion[13:0]), .data(ram_1_data), .sel(decoder_1_out2), .ld(R_W_prime), .clr(Clear));  // open: clk
  // Probe on ram_1_data
  // Probe on ram_1_data
  ROM #(.addrWidth(14), .dataWidth(16)) rom_1 (
    .addr(Direccion[13:0]), .data({ram_1_data, rom_1_data}), .sel(and_2_out));
  ROM #(.addrWidth(14), .dataWidth(16)) rom_2 (
    .addr(Direccion[13:0]), .data({ram_1_data, rom_1_data}), .sel(and_1_out));
  // Probe on {ram_1_data, rom_1_data}
  // Probe on {ram_1_data, rom_1_data}
  RAM #(.addrWidth(14)) ram_3 (
    .addr(Direccion[13:0]), .data(rom_1_data), .sel(decoder_1_out3), .ld(R_W_prime), .clr(Clear));  // open: clk
  RAM #(.addrWidth(14)) ram_4 (
    .addr(Direccion[13:0]), .data(rom_1_data), .sel(decoder_1_out2), .ld(R_W_prime), .clr(Clear));  // open: clk
  // Probe on rom_1_data
  // Probe on rom_1_data
  // Probe on {ram_1_data, rom_1_data}
  // Probe on {ram_1_data, rom_1_data}
  not not_1 (not_1_out, R_W_prime);
  assign {ram_1_data, rom_1_data} = not_1_out ? MDR__Memory_Data_Register : 16'bz;  // Controlled_Buffer controlled_buffer_1

  // Notes on the sheet:
  //   RAM 3 16x8
  //   RAM 1 16x8
  //   ROM 2 16x16
  //   ROM 1 16x16
  //   RAM 4 16x8
  //   RAM 2 16x8
endmodule
