// Logisim project A1_LoroM_Pr1.circ as structural Verilog
module Ej__1_4__pines (
  input  A,
  output F,
  output G,
  output H,
  output I,
  output J
);


  assign F = A;
  assign G = 1'b1;
  assign H = 1'b1;
  assign I = 1'b0;
  assign J = A;

  // Other names for the same wires on the sheet: LongitudDeNombreTest = A
endmodule

module Ej__1_5__E_S (
  input  A,
  output F,
  output G
);

  Button Quiero_ver_cuan_largo_puede_ser_el_nombre (.out(F));
  LED led_1 (.in(A));

  assign G = A;
endmodule
