// Logisim project A1_LoroM_Pr2.circ as structural Verilog
module Ej__2_1__Buses (
  input  [7:0] Entrada,
  output [7:0] Salida
);

  // Probe on Entrada
  // Probe on Entrada
  // Probe on Entrada
  // Probe on Entrada

  assign Salida = Entrada;
endmodule

module Ej__2_2__Ctes (
  output [7:0] Valor_binario
);

  // Probe on 8'hbd

  assign Valor_binario = 8'hbd;

  // Notes on the sheet:
  //   Cte: valor hexadecimal
  //   DNI: 029501730 -> (2+9+5+1+7+3)*7 = 
endmodule

module Ej__2_3__Separa (
  input  [3:0] Entrada,
  output [3:0] Salida__invertida
);


  assign Salida__invertida = {Entrada[0], Entrada[1], Entrada[2], Entrada[3]};
endmodule

module Ej__2_4__Extender (
  output [3:0] Salida_extendida,
  output [3:0] Salida_extendida_2,
  output [3:0] Salida_extendida_3
);

  wire Pulsador_2_out, Pulsador_out;

  Button Pulsador (.out(Pulsador_out));
  Button Pulsador_2 (.out(Pulsador_2_out));
  Button Pulsador_3 (.out(Salida_extendida_3[3]));
  assign Salida_extendida = {{3{Pulsador_out}}, Pulsador_out};  // Bit_Extender bit_extender_1
  assign Salida_extendida_2 = {{3{Pulsador_2_out}}, Pulsador_2_out};  // Bit_Extender bit_extender_2

  assign Salida_extendida_3[2:0] = {3{Salida_extendida_3[3]}};

  // Notes on the sheet:
  //   Usando bit extender #1
  //   Usando bit extender #2
  //   Usando Splitter
endmodule
