// Logisim project Pr3_template.circ as structural Verilog: 3 circuits, main circuit Ej. 3.1: XOR
module Ej__3_1__XOR (
  input  A,
  input  B,
  output f,
  output g
);

  wire and_1_out, and_2_out;

  and and_1 (and_1_out, A, ~B);  // AND_Gate
  and and_2 (and_2_out, ~A, B);  // AND_Gate
  xor xor_1 (f, A, B);
  xor xor_2 (g, and_1_out, and_2_out);
endmodule

module Ej__3_2__XOR_4bits (
  output [3:0] f,
  output [3:0] g
);

  wire [3:0] and_1_out, and_2_out;

  // Probe on 4'b1001
  // Probe on 4'b0101
  assign and_1_out = 4'b1001 & ~4'b0101;  // AND_Gate and_1, 4 bits wide
  assign and_2_out = ~4'b1001 & 4'b0101;  // AND_Gate and_2, 4 bits wide
  assign f = 4'b1001 ^ 4'b0101;  // XOR_Gate xor_1, 4 bits wide
  assign g = and_1_out ^ and_2_out;  // XOR_Gate xor_2, 4 bits wide

  // Notes on the sheet:
  //   A
  //   B
endmodule

module Ej__3_3__Boole (
  input  A,
  input  B,
  output out_3,
  output out_4
);

  wire and_1_out;

  and and_1 (and_1_out, ~A, B);  // AND_Gate
  or or_1 (out_3, and_1_out, A);
  or or_2 (out_4, A, B);

  // Notes on the sheet:
  //   A + A' * B
  //   A + B
  //   T.7: Absorción II
  //   A + A' * B = A + B 
endmodule
