// Logisim project A2_LoroM_Pr4.circ as structural Verilog
module Ej_4_1__CirComb (
  input  A,
  input  B,
  input  C,
  output f,
  output g
);

  wire and_1_out, and_2_out, and_3_out, not_1_out, or_1_out, or_3_out, xor_1_out;

  and and_1 (and_1_out, A, B);
  or or_1 (or_1_out, A, B);
  or or_2 (f, and_1_out, xor_1_out);
  xor xor_1 (xor_1_out, or_1_out, C);
  or or_3 (or_3_out, or_1_out, C);
  and and_2 (and_2_out, and_1_out, C);
  not not_1 (not_1_out, f);
  and and_3 (and_3_out, not_1_out, or_3_out);
  or or_4 (g, and_3_out, and_2_out);
endmodule

module Ej_4_5__Minimizado (
  input  A,
  input  B,
  input  C,
  output f,
  output g
);

  wire and_1_out, and_2_out, and_3_out, and_4_out, and_5_out, and_7_out, and_8_out, and_9_out, and_10_out,
       not_1_out, not_2_out, not_3_out, not_4_out, not_5_out, not_6_out, or_1_out, or_2_out, or_3_out,
       or_4_out, or_5_out;

  or or_1 (or_1_out, A, B);
  or or_2 (or_2_out, A, C);
  not not_1 (not_1_out, A);
  not not_2 (not_2_out, B);
  not not_3 (not_3_out, A);
  not not_4 (not_4_out, B);
  and and_1 (and_1_out, or_1_out, or_2_out);
  or or_3 (or_3_out, B, C);
  and and_2 (and_2_out, not_1_out, not_2_out);
  and and_3 (and_3_out, not_3_out, B);
  not not_5 (not_5_out, C);
  and and_4 (and_4_out, A, not_4_out);
  not not_6 (not_6_out, C);
  and and_5 (and_5_out, A, B);
  and and_6 (f, and_1_out, or_3_out);
  and and_7 (and_7_out, and_2_out, C);
  and and_8 (and_8_out, and_3_out, not_5_out);
  and and_9 (and_9_out, and_4_out, not_6_out);
  and and_10 (and_10_out, and_5_out, C);
  or or_4 (or_4_out, and_7_out, and_8_out);
  or or_5 (or_5_out, and_9_out, and_10_out);
  or or_6 (g, or_4_out, or_5_out);
endmodule

module Ej_4_1__CirComb_TEST (
  input  A,
  input  B,
  input  C,
  output f,
  output g
);

  wire and_1_out, and_2_out, and_3_out, and_4_out, and_5_out, and_6_out, not_1_out, not_2_out, not_3_out,
       not_4_out;

  and and_1 (and_1_out, B, C);
  and and_2 (and_2_out, A, C);
  and and_3 (and_3_out, A, B);
  not not_1 (not_1_out, A);
  not not_2 (not_2_out, C);
  not not_3 (not_3_out, B);
  not not_4 (not_4_out, C);
  or or_1 (f, and_1_out, and_2_out, and_3_out);
  and and_4 (and_4_out, not_1_out, B, not_2_out);
  and and_5 (and_5_out, A, not_3_out, not_4_out);
  and and_6 (and_6_out, A, B, C);
  or or_2 (g, and_4_out, and_5_out, and_6_out);
endmodule

module Ej_4_1__CirComb_TEst2 (
  input  A,
  input  B,
  input  C,
  output f,
  output g
);

  wire and_1_out, and_2_out, and_3_out, not_1_out, not_2_out, not_3_out, or_2_out, or_3_out, or_4_out,
       or_5_out;

  and and_1 (and_1_out, B, C);
  and and_2 (and_2_out, A, C);
  and and_3 (and_3_out, A, B);
  not not_1 (not_1_out, C);
  not not_2 (not_2_out, C);
  not not_3 (not_3_out, C);
  or or_1 (f, and_1_out, and_2_out, and_3_out);
  or or_2 (or_2_out, A, B);
  or or_3 (or_3_out, A, not_1_out);
  or or_4 (or_4_out, B, not_2_out);
  or or_5 (or_5_out, A, B, not_3_out);
  and and_4 (g, or_2_out, or_3_out, or_4_out, or_5_out);
endmodule
