// Logisim project Pr4_template.circ as structural Verilog
module Ej_4_1__CirComb (
  input  in_1,
  input  in_2,
  input  in_3,
  output out_4,
  output out_5
);

  wire and_1_out, and_2_out, and_3_out, and_4_out, not_1_out, or_1_out, or_3_out;

  and and_1 (and_1_out, in_1, in_2);
  or or_1 (or_1_out, in_1, in_2);
  or or_2 (out_4, and_1_out, and_2_out);
  and and_2 (and_2_out, or_1_out, in_3);
  or or_3 (or_3_out, or_1_out, in_3);
  and and_3 (and_3_out, and_1_out, in_3);
  not not_1 (not_1_out, out_4);
  and and_4 (and_4_out, not_1_out, or_3_out);
  or or_4 (out_5, and_4_out, and_3_out);
endmodule
