// Logisim project Pr5_template.circ as structural Verilog: 4 circuits, main circuit Ej 5.2: f,g->MUX 8x1
module MUX_4x1 (
  input  D0,
  input  D1,
  input  D2,
  input  D3,
  input  en,
  input  A,
  input  B,
  output y
);

  wire and_1_out, and_2_out, and_3_out, and_4_out, or_1_out;

  and and_1 (and_1_out, D0, ~A, ~B);  // AND_Gate
  and and_2 (and_2_out, D1, ~A, B);  // AND_Gate
  and and_3 (and_3_out, D2, A, ~B);  // AND_Gate
  and and_4 (and_4_out, D3, A, B);
  or or_1 (or_1_out, and_1_out, and_2_out, and_3_out, and_4_out);
  and and_5 (y, or_1_out, en);
endmodule

module MUX_8x1 (
  input  D0,
  input  D1,
  input  D2,
  input  D3,
  input  D4,
  input  D5,
  input  D6,
  input  D7,
  input  en,
  input  A,
  input  B,
  input  C,
  output y
);

  wire mux_4x1_1_y, mux_4x1_2_y, not_1_out, or_1_out;

  not not_1 (not_1_out, A);
  MUX_4x1 mux_4x1_1 (.D0(D0), .D1(D1), .D2(D2), .D3(D3), .y(mux_4x1_1_y), .en(not_1_out), .A(B), .B(C));
  MUX_4x1 mux_4x1_2 (.D0(D4), .D1(D5), .D2(D6), .D3(D7), .y(mux_4x1_2_y), .en(A), .A(B), .B(C));
  or or_1 (or_1_out, mux_4x1_1_y, mux_4x1_2_y);
  and and_1 (y, or_1_out, en);
endmodule

module Ej_5_2__f_g__MUX_8x1 (
  input  A,
  input  B,
  input  C,
  output f,
  output g
);

  Multiplexer #(.select(3), .disabled(0), .enable("false")) multiplexer_1 (
    .in0(1'b0), .in1(1'b1), .in2(1'b0), .in3(1'b0), .in4(1'b0), .in5(1'b0), .in6(1'b1), .in7(1'b1), .out(f),
    .sel({A, B, C}));
  MUX_8x1 mux_8x1_1 (
    .D0(1'b0), .D1(1'b1), .D2(1'b0), .D3(1'b0), .D4(1'b0), .D5(1'b0), .D6(1'b1), .D7(1'b1), .y(g), .en(1'b1),
    .A(A), .B(B), .C(C));
endmodule

module Ej_5_3__f_g__DEC_3x8 (
  input  A,
  input  B,
  input  C,
  output f,
  output g
);

  wire decoder_1_out0, decoder_1_out1, decoder_1_out2, decoder_1_out4, decoder_1_out6, decoder_1_out7,
       not_1_out, not_2_out, not_3_out, not_4_out;

  Decoder #(.select(3), .disabled(0), .enable("false")) decoder_1 (
    .out0(decoder_1_out0), .out1(decoder_1_out1), .out2(decoder_1_out2), .out4(decoder_1_out4),
    .out6(decoder_1_out6), .out7(decoder_1_out7), .sel({A, B, C}));  // open: out3, out5
  not not_1 (not_1_out, decoder_1_out0);
  not not_2 (not_2_out, decoder_1_out2);
  not not_3 (not_3_out, decoder_1_out4);
  not not_4 (not_4_out, decoder_1_out6);
  or or_1 (f, decoder_1_out1, decoder_1_out6, decoder_1_out7);
  and and_1 (g, not_1_out, not_2_out, not_3_out, not_4_out);
endmodule
