// Logisim project A1_LoroM_Pr6.circ as structural Verilog: 4 circuits, main circuit Ej 6.1: Comple2
module Ej_6_1__Comple2 (
  input  [7:0] A,
  output [7:0] A_2,
  output [7:0] minus_A,
  output [7:0] minus_A_2
);

  wire [7:0] not_1_out;

  assign not_1_out = ~A;  // NOT_Gate not_1, 8 bits wide
  // Probe on A
  // Probe on minus_A
  Adder adder_1 (.a(not_1_out), .b({8{1'b0}}), .out(minus_A), .cin(1'b1));  // open: cout
  Negator negator_1 (.in(A), .out(minus_A_2));
  // Probe on minus_A_2

  assign A_2 = A;
endmodule

module Ej_6_2__SumRest_4b (
  input  S_R_prime,
  input  [3:0] B,
  input  [3:0] A,
  output [3:0] Resultado,
  output Cout,
  output Overflow
);

  wire bit_signo_4b_1_signo, bit_signo_4b_2_signo, bit_signo_4b_3_signo, xnor_1_out, xor_2_out;
  wire [3:0] xor_1_out;

  // Probe on B
  // Probe on A
  assign xor_1_out = {4{S_R_prime}} ^ B;  // XOR_Gate xor_1, 4 bits wide
  Bit_signo__4b bit_signo_4b_1 (.in(xor_1_out), .signo(bit_signo_4b_1_signo));
  Bit_signo__4b bit_signo_4b_2 (.in(A), .signo(bit_signo_4b_2_signo));
  // Probe on Resultado
  Adder #(.width(4)) adder_1 (.a(xor_1_out), .b(A), .out(Resultado), .cin(S_R_prime), .cout(Cout));
  Bit_signo__4b bit_signo_4b_3 (.in(Resultado), .signo(bit_signo_4b_3_signo));
  xnor xnor_1 (xnor_1_out, bit_signo_4b_1_signo, bit_signo_4b_2_signo);
  xor xor_2 (xor_2_out, bit_signo_4b_3_signo, bit_signo_4b_1_signo);
  and and_1 (Overflow, xor_2_out, xnor_1_out);
endmodule

module Bit_signo__4b (
  input  [3:0] in,
  output signo
);

  BitSelector #(.width(4)) bitselector_1 (.in(in), .out(signo), .sel(2'b11));
endmodule

module Ej_6_4__CompBits1 (
  input  [3:0] A,
  input  [3:0] B,
  output [3:0] S
);

  wire comparator_1_lt, comparator_2_eq, comparator_2_lt, not_1_out;
  wire [2:0] bitadder_1_out, bitadder_2_out;
  wire [3:0] multiplexer_1_out, multiplexer_2_out;

  Comparator #(.width(4), .mode("unsigned")) comparator_1 (.a(A), .b(B), .lt(comparator_1_lt));  // open: gt, eq
  BitAdder #(.width(4)) bitadder_1 (.in0(A), .out(bitadder_1_out));
  Comparator #(.width(3), .mode("unsigned")) comparator_2 (
    .a(bitadder_1_out), .b(bitadder_2_out), .eq(comparator_2_eq), .lt(comparator_2_lt));  // open: gt
  BitAdder #(.width(4)) bitadder_2 (.in0(B), .out(bitadder_2_out));
  Multiplexer #(.width(4), .disabled(0)) multiplexer_1 (
    .in0(A), .in1(B), .out(multiplexer_1_out), .sel(comparator_1_lt), .en(comparator_2_eq));
  Multiplexer #(.width(4), .disabled(0), .enable("false")) multiplexer_2 (
    .in0(A), .in1(B), .out(multiplexer_2_out), .sel(comparator_2_lt));
  Multiplexer #(.width(4), .disabled(0), .enable("false")) multiplexer_3 (
    .in0(multiplexer_1_out), .in1(multiplexer_2_out), .out(S), .sel(not_1_out));
  not not_1 (not_1_out, comparator_2_eq);

  // Notes on the sheet:
  //   (B>A)
  //   Mayor (A,B)
  //   Mas bits activos (A,B)
endmodule
