// Logisim project Pr6_template.circ as structural Verilog: 4 circuits, main circuit Ej 6.1: Comple2
module Ej_6_1__Comple2 (
  input  [7:0] A,
  output [7:0] A_2,
  output [7:0] minus_A,
  output [7:0] minus_A_2
);

  wire [7:0] not_1_out;

  assign not_1_out = ~A;  // NOT_Gate not_1, 8 bits wide
  // Probe on A
  // Probe on minus_A
  Adder adder_1 (.a(not_1_out), .b({8{1'b0}}), .out(minus_A), .cin(1'b1));  // open: cout
  Negator negator_1 (.in(A), .out(minus_A_2));
  // Probe on minus_A_2

  assign A_2 = A;
endmodule

module Ej_6_2__SumRest_4b (
  input  S_R_prime,
  input  [3:0] B,
  input  [3:0] A,
  output [3:0] Resultado,
  output Cout,
  output Overflow
);

  wire [3:0] xor_1_out;

  // Probe on B
  // Probe on A
  assign xor_1_out = B;  // XOR_Gate xor_1, 4 bits wide XOR_Gate
  Bit_signo__4b bit_signo_4b_1 ();  // open: in, signo
  Bit_signo__4b bit_signo_4b_2 ();  // open: in, signo
  // Probe on Resultado
  Adder #(.width(4)) adder_1 (.a(xor_1_out), .b(A), .out(Resultado), .cout(Cout));  // open: cin
  Bit_signo__4b bit_signo_4b_3 (.in(Resultado));  // open: signo
  // AND_Gate and_1 has open pins: out=Overflow
endmodule

module Bit_signo__4b (
  input  [3:0] in,
  output signo
);
endmodule

module Ej_6_4__CompBits1 (
  input  [3:0] A,
  input  [3:0] B,
  output [3:0] S
);

  wire comparator_1_lt;
  wire [2:0] bitadder_1_out, bitadder_2_out;

  Comparator #(.width(4), .mode("unsigned")) comparator_1 (.a(A), .b(B), .lt(comparator_1_lt));  // open: gt, eq
  BitAdder #(.width(4)) bitadder_1 (.in0(A), .out(bitadder_1_out));
  Comparator #(.width(3), .mode("unsigned")) comparator_2 (.a(bitadder_1_out), .b(bitadder_2_out));  // open: gt, eq, lt
  BitAdder #(.width(4)) bitadder_2 (.in0(B), .out(bitadder_2_out));

  // Notes on the sheet:
  //   (B>A)
  //   Mayor (A,B)
  //   Mas bits activos (A,B)
endmodule
