// Logisim project A1_LoroM_Pr7.circ as structural Verilog: 3 circuits, main circuit Ej 7.2: Biestables
module Ej_7_1__Elevador_comb (
  input  v,
  input  FC_abajo,
  input  Encendido,
  input  FC_arriba,
  input  in_5
);

  wire and_1_out, and_2_out, and_3_out, and_4_out, button_out, or_1_out, or_2_out, v_out;

  Button u_v (.out(v_out));
  or or_1 (or_1_out, v_out, v);
  Button button (.out(button_out));
  or or_2 (or_2_out, button_out, in_5);
  and and_1 (and_1_out, or_1_out, ~or_2_out, Encendido);  // AND_Gate
  and and_2 (and_2_out, Encendido, or_2_out);
  LED Motor_v (.in(and_3_out));
  and and_3 (and_3_out, and_1_out, ~FC_abajo);  // AND_Gate
  and and_4 (and_4_out, ~FC_arriba, and_2_out);  // AND_Gate
  LED Motor (.in(and_4_out));
endmodule

module Ej_7_2__Biestables (
  input  in_1,
  input  in_2,
  input  in_3,
  input  in_4,
  output D,
  output T,
  output J_K
);

  wire CLK_out, Clr_out, en_out, not_1_out, Pre_out;

  Clock CLK (.out(CLK_out));
  Button Pre (.out(Pre_out));
  Button en (.out(en_out));
  Button Clr (.out(Clr_out));
  not not_1 (not_1_out, en_out);
  D_Flip_Flop #(.trigger("high")) d_ff_1 (
    .clk(CLK_out), .D(in_2), .Q(D), .preset(Pre_out), .en(not_1_out), .reset(Clr_out));  // open: Qn
  T_Flip_Flop #(.trigger("falling")) t_ff_1 (
    .clk(CLK_out), .T(in_3), .Q(T), .preset(Pre_out), .reset(Clr_out), .en(not_1_out));  // open: Qn
  J_K_Flip_Flop j_k_ff_1 (
    .J(in_1), .clk(CLK_out), .K(in_4), .Q(J_K), .preset(Pre_out), .en(not_1_out), .reset(Clr_out));  // open: Qn
endmodule

module Ej_7_4__Elevador_sec___J_K (
  input  in_1,
  input  FC_abajo,
  input  Encendido,
  input  in_4,
  input  FC_arriba
);

  wire and_1_out, and_2_out, and_3_out, button_out, CLK_out, j_k_ff_1_q, j_k_ff_1_qn, j_k_ff_2_q,
       j_k_ff_2_qn, or_1_out, or_2_out, v_out;

  Button v (.out(v_out));
  Button button (.out(button_out));
  or or_1 (or_1_out, v_out, in_1);
  and and_1 (and_1_out, or_1_out, ~or_2_out, Encendido);  // AND_Gate
  and and_2 (and_2_out, Encendido, or_2_out);
  or or_2 (or_2_out, button_out, in_4);
  Clock CLK (.out(CLK_out));
  and and_3 (and_3_out, j_k_ff_1_qn, j_k_ff_2_qn);
  J_K_Flip_Flop j_k_ff_1 (
    .J(and_1_out), .clk(CLK_out), .K(and_2_out), .Q(j_k_ff_1_q), .Qn(j_k_ff_1_qn), .en(and_3_out),
    .reset(FC_abajo));  // open: preset
  J_K_Flip_Flop j_k_ff_2 (
    .J(and_2_out), .clk(CLK_out), .K(and_1_out), .Q(j_k_ff_2_q), .Qn(j_k_ff_2_qn), .en(and_3_out),
    .reset(FC_arriba));  // open: preset
  LED Motor_v (.in(j_k_ff_1_q));
  LED Motor (.in(j_k_ff_2_q));
endmodule
