// Logisim project Pr7_template.circ as structural Verilog: 3 circuits, main circuit Ej 7.2: Biestables
module Ej_7_1__Elevador_comb (
  input  FC_abajo,
  input  Encendido,
  input  FC_arriba
);

  wire and_3_out, and_4_out;

  Button v ();  // open: out
  Button button ();  // open: out
  // AND_Gate and_1 is placed but not wired
  // AND_Gate and_2 is placed but not wired
  LED Motor_v (.in(and_3_out));
  // AND_Gate and_3 has open pins: out=and_3_out
  // AND_Gate and_4 has open pins: out=and_4_out
  LED Motor (.in(and_4_out));
endmodule

module Ej_7_2__Biestables (
);

  wire en_out;

  Clock CLK ();  // open: out
  Button Pre ();  // open: out
  Button en (.out(en_out));
  Button Clr ();  // open: out
  // NOT_Gate not_1 has open pins: in=en_out, out=open
  D_Flip_Flop d_ff_1 ();  // open: clk, D, Q, Qn, preset, en, reset
  T_Flip_Flop t_ff_1 ();  // open: clk, T, Q, Qn, preset, reset, en
  J_K_Flip_Flop j_k_ff_1 ();  // open: J, clk, K, Q, Qn, preset, en, reset
endmodule

module Ej_7_4__Elevador_sec___J_K (
  input  FC_abajo,
  input  Encendido,
  input  FC_arriba
);

  wire button_out, CLK_out, j_k_ff_1_q, j_k_ff_2_q, v_out;

  Button v (.out(v_out));
  // AND_Gate and_1 has open pins: in0=v_out, in1=button_out, in2=Encendido, out=open
  // AND_Gate and_2 has open pins: in0=Encendido, in1=button_out, out=open
  Button button (.out(button_out));
  Clock CLK (.out(CLK_out));
  LED Motor_v (.in(j_k_ff_1_q));
  J_K_Flip_Flop j_k_ff_1 (.Q(j_k_ff_1_q));  // open: J, clk, K, Qn, preset, en, reset
  J_K_Flip_Flop j_k_ff_2 (.Q(j_k_ff_2_q));  // open: J, clk, K, Qn, preset, en, reset
  LED Motor (.in(j_k_ff_2_q));
endmodule
