// Logisim project A1_LoroM_Pr8.circ as structural Verilog: 4 circuits, main circuit Ej 8.1: Register
module Ej_8_1__Register (
  input  [3:0] Dato,
  input  en,
  output [3:0] Salida
);

  wire CLK_out, CLR_out;

  // Probe on Dato
  Clock CLK (.out(CLK_out));
  Button CLR (.out(CLR_out));
  // Probe on Salida
  Register #(.width(4)) Registro (.D(Dato), .en(en), .Q(Salida), .clk(CLK_out), .clr(CLR_out));
endmodule

module Ej_8_2__Ring_cnt (
  input  [3:0] in_1,
  output [3:0] Salida,
  output [3:0] Salida_2
);

  wire CLK_out, CLR_out, LD_out, not_1_out, Ring_CNT_2_out, Ring_CNT_out;

  Button LD (.out(LD_out));
  Shift_Register #(.length(4)) Ring_CNT (
    .in(Ring_CNT_out), .clk(CLK_out), .out(Ring_CNT_out), .load(LD_out), .clr(CLR_out), .d0(in_1[3]),
    .q0(Salida[3]), .d1(in_1[2]), .q1(Salida[2]), .d2(in_1[1]), .q2(Salida[1]), .d3(in_1[0]), .q3(Salida[0]));  // open: shift
  Clock CLK (.out(CLK_out));
  Button CLR (.out(CLR_out));
  Shift_Register #(.length(4)) Ring_CNT_2 (
    .in(not_1_out), .clk(CLK_out), .out(Ring_CNT_2_out), .clr(CLR_out), .q0(Salida_2[3]), .q1(Salida_2[2]),
    .q2(Salida_2[1]), .q3(Salida_2[0]));  // open: shift, load, d0, d1, d2, d3
  not not_1 (not_1_out, Ring_CNT_2_out);
endmodule

module Ej_8_3__CntMOD_25 (
);

  wire button_out, CLK_out, counter_1_carry, d_ff_1_q, or_1_out;
  wire [7:0] counter_1_q;

  Clock CLK (.out(CLK_out));
  Button button (.out(button_out));
  or or_1 (or_1_out, button_out, d_ff_1_q);
  D_Flip_Flop d_ff_1 (.clk(CLK_out), .D(or_1_out), .Q(d_ff_1_q), .reset(counter_1_carry));  // open: Qn, preset, en
  // Probe on counter_1_q
  Counter #(.max('h19), .ongoal("stay")) counter_1 (
    .count(d_ff_1_q), .Q(counter_1_q), .carry(counter_1_carry), .clk(CLK_out), .clr(counter_1_carry));  // open: load, D
  LED \Acción_temporizada  (.in(d_ff_1_q));

  // Notes on the sheet:
  //   Start
endmodule

module Ej_8_4__Lavadora (
  output [3:0] Salida
);

  wire clock_1_out, counter_1_carry, d_ff_1_q, or_1_out, or_2_out, Start_out, Stop_out;
  wire [3:0] Address;

  Button Start (.out(Start_out));
  Button Stop (.out(Stop_out));
  or or_1 (or_1_out, Stop_out, counter_1_carry);
  Clock clock_1 (.out(clock_1_out));
  or or_2 (or_2_out, Start_out, d_ff_1_q);
  D_Flip_Flop d_ff_1 (.clk(clock_1_out), .D(or_2_out), .Q(d_ff_1_q), .reset(or_1_out));  // open: Qn, preset, en
  // Probe on Salida
  ROM #(.addrWidth(4), .dataWidth(4)) rom_1 (.addr(Address), .data(Salida));  // open: sel
  Counter #(.width(4), .max('he), .ongoal("load")) counter_1 (
    .count(d_ff_1_q), .Q(Address), .carry(counter_1_carry), .clk(clock_1_out), .clr(or_1_out));  // open: load, D
  LED Carga_agua (.in(Salida[0]));
  LED Gira_tambor (.in(Salida[1]));
  LED Desagua (.in(Salida[2]));
  LED Toma_detergente (.in(Salida[3]));

  // Notes on the sheet:
  //   contents of rom_1 (hex, n*v repeats v):
  //   0 1 2 4 9 2 4 1 2 4 1 2 4 2
endmodule
