// Logisim project Pr8_template.circ as structural Verilog: 4 circuits, main circuit Ej 8.1: Register
module Ej_8_1__Register (
  input  [3:0] Dato,
  input  en,
  output [3:0] Salida
);

  Button CLR ();  // open: out
  Register #(.width(4)) Registro (.D(Dato), .en(en), .Q(Salida));  // open: clk, clr
  Clock CLK ();  // open: out
endmodule

module Ej_8_2__Ring_cnt (
  output [3:0] Salida
);

  wire [3:0] undriven;

  Button LD ();  // open: out
  Button CLR ();  // open: out
  Shift_Register #(.length(4)) Ring_CNT (
    .d0(undriven[3]), .q0(Salida[3]), .d1(undriven[2]), .q1(Salida[2]), .d2(undriven[1]), .q2(Salida[1]),
    .d3(undriven[0]), .q3(Salida[0]));  // open: shift, in, clk, out, load, clr
  Clock CLK ();  // open: out
endmodule

module Ej_8_3__CntMOD_25 (
);

  wire button_out, d_ff_1_q, or_1_out;

  Clock CLK ();  // open: out
  Button button (.out(button_out));
  or or_1 (or_1_out, button_out, d_ff_1_q);
  D_Flip_Flop d_ff_1 (.D(or_1_out), .Q(d_ff_1_q));  // open: clk, Qn, preset, en, reset
  // Probe on nothing
  Counter counter_1 ();  // open: load, D, count, Q, carry, clk, clr
  LED \Acción_temporizada  ();  // open: in

  // Notes on the sheet:
  //   Start
endmodule

module Ej_8_4__Lavadora (
  output [3:0] Salida
);

  wire d_ff_1_q;
  wire [3:0] Address;

  Button Start ();  // open: out
  Button Stop ();  // open: out
  Clock clock_1 ();  // open: out
  D_Flip_Flop d_ff_1 (.Q(d_ff_1_q));  // open: clk, D, Qn, preset, en, reset
  // Probe on Salida
  ROM #(.addrWidth(4), .dataWidth(4)) rom_1 (.addr(Address), .data(Salida));  // open: sel
  Counter #(.width(4), .max('hd), .ongoal("load")) counter_1 (
    .count(d_ff_1_q), .Q(Address));  // open: load, D, carry, clk, clr
  LED Carga_agua (.in(Salida[0]));
  LED Gira_tambor (.in(Salida[1]));
  LED Desagua (.in(Salida[2]));
  LED Toma_detergente (.in(Salida[3]));
endmodule
