// Logisim project 1A_GouramAdam_LoroMarcos.circ as structural Verilog: 3 circuits, main circuit main
module main (
);

  wire Clock_out, Inicio_out;
  wire [2:0] Contador_Mod5_q0, Decodificador_s0;

  Clock Clock (.out(Clock_out));
  Button Inicio (.out(Inicio_out));
  Cont_mod_5 Contador_Mod5 (
    .clock(Clock_out), .inicio(Inicio_out), .Q0(Contador_Mod5_q0[0]), .Q1(Contador_Mod5_q0[1]),
    .Q2(Contador_Mod5_q0[2]));
  Hex_Digit_Display hex_digit_display_1 (.value({1'b0, Contador_Mod5_q0}));  // open: dp
  Circ_deco Decodificador (
    .Q0(Contador_Mod5_q0[0]), .Q1(Contador_Mod5_q0[1]), .Q2(Contador_Mod5_q0[2]), .S0(Decodificador_s0[0]),
    .S1(Decodificador_s0[1]), .S2(Decodificador_s0[2]));
  Hex_Digit_Display hex_digit_display_2 (.value({1'b0, Decodificador_s0}));  // open: dp

  // Notes on the sheet:
  //   DNI elegido: 05989404C
  //   Secuencia de estados asignada: 6, 3, 4, 3, 7
  //   Numeros asignados de FFs para el contador mod 5: 3, 2, 2
  //   Numeros asignados para implementacion entradas a FF: 3, 2, 2
  //   DISEÑA AQUI EL MAIN
  //   DNI del compañero: 06623096Q
  //   Dígito del contador
  //   Dígito de la secuencia
endmodule

module Cont_mod_5 (
  input  clock,
  input  inicio,
  output Q0,
  output Q1,
  output Q2
);

  wire decoder_1_out3, decoder_1_out4, multiplexer_1_out, multiplexer_2_out, or_1_out;

  Multiplexer #(.select(3), .enable("false")) multiplexer_1 (
    .in0(1'b1), .in1(1'b1), .in2(1'b1), .in3(1'b1), .in4(1'b0), .out(multiplexer_1_out), .sel({Q2, Q1, Q0}));  // open: in5, in6, in7
  Multiplexer #(.select(3), .enable("false")) multiplexer_2 (
    .in0(1'b0), .in1(1'b1), .in2(1'b0), .in3(1'b1), .in4(1'b0), .out(multiplexer_2_out), .sel({Q2, Q1, Q0}));  // open: in5, in6, in7
  Decoder #(.select(3), .enable("false")) decoder_1 (
    .out3(decoder_1_out3), .out4(decoder_1_out4), .sel({Q2, Q1, Q0}));  // open: out0, out1, out2, out5, out6, out7
  J_K_Flip_Flop j_k_ff_1 (
    .J(multiplexer_1_out), .clk(clock), .K(multiplexer_1_out), .Q(Q0), .reset(inicio));  // open: Qn, preset, en
  J_K_Flip_Flop j_k_ff_2 (
    .J(multiplexer_2_out), .clk(clock), .K(multiplexer_2_out), .Q(Q1), .reset(inicio));  // open: Qn, preset, en
  T_Flip_Flop t_ff_1 (.clk(clock), .T(or_1_out), .Q(Q2), .reset(inicio));  // open: Qn, preset, en
  or or_1 (or_1_out, decoder_1_out3, decoder_1_out4);

  // Notes on the sheet:
  //   Condiciones de no importa ->
  //   Condiciones de no importa ->
endmodule

module Circ_deco (
  input  Q0,
  input  Q1,
  input  Q2,
  output S0,
  output S1,
  output S2
);

  or or_1 (S0, Q0, Q2);
  or or_2 (S1, Q0, ~Q1);  // OR_Gate
  not not_1 (S2, Q0);

  // Notes on the sheet:
  //   Q0 + Q2
  //   Q0 + ~Q1
  //   ~Q0
endmodule
