// Logisim project Template.circ as structural Verilog
module main (
);


  // Notes on the sheet:
  //   DNI elegido:
  //   Secuencia de estados asignada:
  //   Numeros asignados de FFs para el contador mod 5:
  //   Numeros asignados para implementacion entradas a FF:
  //   DISEÑA AQUI EL MAIN
  //   DNI del compañero:
endmodule
